# Fritzing sketch Монтажная схема (saved by Fritzing 0.9.10b)

parts:
  M1 = Stepper Motor - Bipolar
  M2 = Stepper Motor - Bipolar
  M3 = Stepper Motor - Bipolar
  Pololu_A1 = Pololu A4988 [package=SO16]
  Pololu_A2 = Pololu A4988 [package=SO16]
  Pololu_A3 = Pololu A4988 [package=SO16]
  VCC1 = Battery
  S1 = Toggle Switch [package=THT]
  U2 = LM2596 step down module
  CPU1 = NodeMCU WROOM ESP 32  # not connected
  A1 = DORHEA ESP32 GPIO breakout board 30pin
  J2 = Basic Servo  # not connected
  J3 = Basic Servo  # not connected
  TCRT1 = TCRT5000 sensor module [part_number=151608]
  TCRT2 = TCRT5000 sensor module [part_number=151608]
  TCRT3 = TCRT5000 sensor module [part_number=151608]
  TCRT4 = TCRT5000 sensor module [part_number=151608]

nets:
  N1: M1.A, Pololu_A3.2B
  N2: M1.C, Pololu_A3.1B
  N3: M1.B, Pololu_A3.2A
  N4: M1.D, Pololu_A3.1A
  N5: M2.A, Pololu_A2.2B
  N6: M2.C, Pololu_A2.1B
  N7: M2.B, Pololu_A2.2A
  N8: M2.D, Pololu_A2.1A
  N9: M3.A, Pololu_A1.2B
  N10: M3.C, Pololu_A1.1B
  N11: M3.B, Pololu_A1.2A
  N12: M3.D, Pololu_A1.1A
  N13: Pololu_A1.STEP, A1.Pin_75, A1.Pin_122
  N14: Pololu_A1.DIR, A1.Pin_76, A1.Pin_123
  N15: Pololu_A1.VMOT, Pololu_A2.VMOT, Pololu_A3.VMOT, S1.L1, S1.COM, S1.L2, U2.IN+
  N16: Pololu_A2.STEP, A1.Pin_73, A1.Pin_120
  N17: Pololu_A2.DIR, A1.Pin_74, A1.Pin_121
  N18: Pololu_A2.GND#8, VCC1.-, U2.IN-, U2.OUT-, A1.Pin_36, A1.Pin_37, A1.Pin_38, A1.Pin_39, A1.Pin_57, A1.Pin_58, A1.Pin_67, A1.Pin_85, TCRT1.D-, TCRT2.D-, TCRT2.T-, TCRT3.D-, TCRT4.D-
  N19: Pololu_A2.VDD, A1.Pin_59, A1.Pin_60, A1.Pin_63, TCRT4.T+
  N20: Pololu_A3.STEP, A1.Pin_71, A1.Pin_118
  N21: Pololu_A3.DIR, A1.Pin_72, A1.Pin_119
  N22: U2.OUT+, A1.Pin_86
  N23: A1.Pin_10, A1.Pin_49, TCRT1.D+
  N24: A1.Pin_11, A1.Pin_50, TCRT2.D+
  N25: A1.Pin_12, A1.Pin_51, TCRT3.D+
  N26: A1.Pin_13, A1.Pin_52, TCRT4.D+

notes:
  Nema 17
  Шаговый двигатель
  Управление перистальтическим насосом №1
  12в; 1,5а
  Nema 17
  Шаговый двигатель
  Управление перистальтическим насосом №2
  12в; 1,5а здесь]
  Nema 17
  Шаговый двигатель
  Управление перистальтическим насосом №3
  12в; 1,5а
  MG995
  Сервопривод
  вращение диспенсера
  Угол(max) -180 градусов
  MG995
  Сервопривод
  вращение диска со стаканами
  Угол(max) -180 градусов
  Аккумуляторная батарея
  Питание схемы
  12в, 2а
  A4988
  Драйвер шапгового двигателя
  ESP-WROOM-32 Devkit 30p
  Реализует алгоритмы системы
  Питание от LM2596
  TCRT5000
  Датчики отражения(4шт)
  Определяют наличие стаканов
  3.3-5в
  LM2596
  Понижающий преобразователь
  Питает печатную плату
  12в преобразовывает в 5

custom parts:
  LM2596 step down module: LM2596 DC-DC step down power supply module 3 A.
  NodeMCU WROOM ESP 32: 30 pol Development Kit
  DORHEA ESP32 GPIO breakout board 30pin: ESP32 shield 30P expansion board, supports two power supply : DC 6.5-16v and USB 5.V
  TCRT5000 sensor module: breakout board with TCRT5000
